// Logisim project async_lib.circ as structural Verilog: 15 circuits, main circuit network
module neuron (
  input  data_in,
  input  req_in,
  input  rst,
  input  ack_out,
  output ack_in,
  output data_out,
  output req_out
);

  wire ack_out_t, and_1_out, comparator_1_gt, ctrl1, ctrl2, ctrl3, ctrl4, ctrl5, ctrl6, ctrl_1_req_out,
       ctrl_2_ack_in, ctrl_2_req_out, ctrl_3_ack_in, ctrl_3_req_out, ctrl_4_ack_in, ctrl_4_req_out,
       ctrl_5_ack_in, ctrl_rst_on_1_ack_in, ctrl_rst_on_1_req_out, delay_1bit_1_out_1bit1,
       delay_1bit_2_out_1bit1, delay_1bit_3_out_1bit1, fork_1_ack_in, fork_1_req_out1, fork_1_req_out2,
       join_1_ack_in1, join_1_ack_in2, join_1_req_out, not_1_out, register_1_q, req_out_t;
  wire [3:0] adder_1_out, multiplexer_1_out, multiplexer_2_out, register_2_q, register_3_q, register_4_q,
       register_5_q;

  Register #(.width(1)) register_1 (.D(data_in), .Q(register_1_q), .clk(ctrl1), .clr(rst));  // open: en
  ctrl ctrl_1 (
    .req_in(req_in), .ack_in(ack_in), .req_out(ctrl_1_req_out), .ack_out(ctrl_2_ack_in), .ctrl_out(ctrl1),
    .rst(rst));
  not not_1 (not_1_out, data_out);
  and and_1 (and_1_out, not_1_out, req_out_t);
  and and_2 (req_out, req_out_t, data_out);
  or or_1 (ack_out_t, and_1_out, ack_out);
  delay_1bit delay_1bit_1 (.in_1bit(ctrl_1_req_out), .delay(4'b1111), .out_1bit1(delay_1bit_1_out_1bit1));
  Multiplexer #(.width(4), .enable("false")) multiplexer_1 (
    .in0(4'b0000), .in1(4'b0100), .out(multiplexer_1_out), .sel(register_1_q));
  Register #(.width(4)) register_2 (.D(register_5_q), .Q(register_2_q), .clk(ctrl2), .clr(rst));  // open: en
  Register #(.width(4)) register_3 (.D(multiplexer_1_out), .Q(register_3_q), .clk(ctrl3), .clr(rst));  // open: en
  ctrl_rst_on ctrl_rst_on_1 (
    .req_in(ctrl_4_req_out), .ack_in(ctrl_rst_on_1_ack_in), .req_out(ctrl_rst_on_1_req_out),
    .ack_out(join_1_ack_in1), .ctrl_out(ctrl2), .rst(rst));
  ctrl ctrl_2 (
    .req_in(delay_1bit_1_out_1bit1), .ack_in(ctrl_2_ack_in), .req_out(ctrl_2_req_out),
    .ack_out(join_1_ack_in2), .ctrl_out(ctrl3), .rst(rst));
  \join  join_1 (
    .req_in1(ctrl_rst_on_1_req_out), .req_in2(ctrl_2_req_out), .ack_in1(join_1_ack_in1),
    .ack_in2(join_1_ack_in2), .req_out(join_1_req_out), .rst(rst), .ack_out(ctrl_3_ack_in));
  Adder #(.width(4)) adder_1 (.a(register_2_q), .b(register_3_q), .out(adder_1_out));  // open: cin, cout
  delay_1bit delay_1bit_2 (.in_1bit(join_1_req_out), .delay(4'b1111), .out_1bit1(delay_1bit_2_out_1bit1));
  Register #(.width(4)) register_4 (.D(adder_1_out), .Q(register_4_q), .clk(ctrl4), .clr(rst));  // open: en
  ctrl ctrl_3 (
    .req_in(delay_1bit_2_out_1bit1), .ack_in(ctrl_3_ack_in), .req_out(ctrl_3_req_out),
    .ack_out(fork_1_ack_in), .ctrl_out(ctrl4), .rst(rst));
  // Probe on register_4_q
  delay_1bit delay_1bit_3 (.in_1bit(ctrl_3_req_out), .delay(4'b1111), .out_1bit1(delay_1bit_3_out_1bit1));
  Comparator #(.width(4), .mode("unsigned")) comparator_1 (
    .a(register_4_q), .b(4'b1010), .gt(comparator_1_gt));  // open: eq, lt
  \fork  fork_1 (
    .ack_out1(ctrl_4_ack_in), .ack_out2(ctrl_5_ack_in), .req_out1(fork_1_req_out1),
    .req_out2(fork_1_req_out2), .ack_in(fork_1_ack_in), .req_in(delay_1bit_3_out_1bit1), .rst(rst));
  Multiplexer #(.width(4), .enable("false")) multiplexer_2 (
    .in0(register_4_q), .in1(4'b0000), .out(multiplexer_2_out), .sel(comparator_1_gt));
  Register #(.width(4)) register_5 (.D(multiplexer_2_out), .Q(register_5_q), .clk(ctrl5), .clr(rst));  // open: en
  Register #(.width(1)) register_6 (.D(comparator_1_gt), .Q(data_out), .clk(ctrl6), .clr(rst));  // open: en
  ctrl ctrl_4 (
    .req_in(fork_1_req_out1), .ack_in(ctrl_4_ack_in), .req_out(ctrl_4_req_out),
    .ack_out(ctrl_rst_on_1_ack_in), .ctrl_out(ctrl5), .rst(rst));
  ctrl ctrl_5 (
    .req_in(fork_1_req_out2), .ack_in(ctrl_5_ack_in), .req_out(req_out_t), .ack_out(ack_out_t),
    .ctrl_out(ctrl6), .rst(rst));

  // Notes on the sheet:
  //   Zero
  //   Weight
  //   V_thrs
endmodule

module muller (
  input  A,
  input  B,
  input  Reset,
  output Z
);

  wire and_1_out, and_2_out, multiplexer_1_out, multiplexer_2_out, not_1_out, or_1_out, or_2_out;

  Multiplexer multiplexer_1 (.in0(A), .in1(1'b0), .out(multiplexer_1_out), .sel(Reset));  // open: en
  Multiplexer multiplexer_2 (.in0(B), .in1(1'b1), .out(multiplexer_2_out), .sel(Reset));  // open: en
  and and_1 (and_1_out, multiplexer_1_out, multiplexer_2_out);
  or or_1 (or_1_out, multiplexer_1_out, multiplexer_2_out);
  or or_2 (or_2_out, and_1_out, and_2_out);
  and and_2 (and_2_out, or_2_out, or_1_out);
  not not_1 (not_1_out, Reset);
  and and_3 (Z, or_2_out, not_1_out);
endmodule

module muller_inv (
  input  A,
  input  B,
  input  Reset,
  output Z
);

  wire and_1_out, and_2_out, multiplexer_1_out, multiplexer_2_out, not_1_out, not_2_out, or_1_out, or_2_out;

  Multiplexer multiplexer_1 (.in0(A), .in1(1'b0), .out(multiplexer_1_out), .sel(Reset));  // open: en
  Multiplexer multiplexer_2 (.in0(B), .in1(1'b1), .out(multiplexer_2_out), .sel(Reset));  // open: en
  not not_1 (not_1_out, multiplexer_2_out);
  and and_1 (and_1_out, multiplexer_1_out, not_1_out);
  or or_1 (or_1_out, multiplexer_1_out, not_1_out);
  or or_2 (or_2_out, and_1_out, and_2_out);
  and and_2 (and_2_out, or_2_out, or_1_out);
  not not_2 (not_2_out, Reset);
  and and_3 (Z, or_2_out, not_2_out);
endmodule

module p_muller (
  input  A,
  input  B,
  input  Reset,
  output Z
);

  wire and_1_out, and_2_out, multiplexer_1_out, multiplexer_2_out, not_1_out, or_1_out, or_2_out;

  Multiplexer multiplexer_1 (.in0(A), .in1(1'b0), .out(multiplexer_1_out), .sel(Reset));  // open: en
  Multiplexer multiplexer_2 (.in0(B), .in1(1'b1), .out(multiplexer_2_out), .sel(Reset));  // open: en
  and and_1 (and_1_out, multiplexer_1_out, multiplexer_2_out);
  or or_1 (or_1_out, multiplexer_1_out, multiplexer_2_out);
  or or_2 (or_2_out, and_1_out, and_2_out);
  and and_2 (and_2_out, or_2_out, or_1_out);
  not not_1 (not_1_out, Reset);
  and and_3 (Z, or_2_out, not_1_out);
endmodule

module p_muller_inv (
  input  A,
  input  B,
  input  Reset,
  output Z
);

  wire and_1_out, and_2_out, multiplexer_1_out, multiplexer_2_out, not_1_out, not_2_out, or_1_out, or_2_out;

  Multiplexer multiplexer_1 (.in0(A), .in1(1'b0), .out(multiplexer_1_out), .sel(Reset));  // open: en
  Multiplexer multiplexer_2 (.in0(B), .in1(1'b1), .out(multiplexer_2_out), .sel(Reset));  // open: en
  not not_1 (not_1_out, multiplexer_2_out);
  and and_1 (and_1_out, multiplexer_1_out, not_1_out);
  or or_1 (or_1_out, multiplexer_1_out, not_1_out);
  or or_2 (or_2_out, and_1_out, and_2_out);
  and and_2 (and_2_out, or_2_out, or_1_out);
  not not_2 (not_2_out, Reset);
  and and_3 (Z, or_2_out, not_2_out);
endmodule

module \join  (
  input  req_in1,
  input  req_in2,
  input  ack_out,
  input  rst,
  output req_out,
  output ack_in1,
  output ack_in2
);

  p_muller p_muller_1 (.A(req_in1), .B(req_in2), .Reset(rst), .Z(req_out));

  assign ack_in1 = ack_out;
  assign ack_in2 = ack_out;
endmodule

module ctrl (
  input  req_in,
  input  ack_out,
  input  rst,
  output ctrl_out,
  output req_out,
  output ack_in
);

  muller_inv muller_inv_1 (.A(req_in), .B(ack_out), .Reset(rst), .Z(ack_in));

  assign ctrl_out = ack_in;
  assign req_out = ack_in;
endmodule

module \fork  (
  input  ack_out1,
  input  ack_out2,
  input  req_in,
  input  rst,
  output ack_in,
  output req_out1,
  output req_out2
);

  p_muller p_muller_1 (.A(ack_out1), .B(ack_out2), .Reset(rst), .Z(ack_in));

  assign req_out1 = req_in;
  assign req_out2 = req_in;
endmodule

module delay_4bits (
  input  [3:0] in_4bits,
  input  [3:0] delay,
  output [3:0] out_4bits
);

  wire clock_1_out, comparator_1_gt, d_ff_1_q;
  wire [3:0] adder_1_out, register_1_q;

  Clock clock_1 (.out(clock_1_out));
  Adder #(.width(4)) adder_1 (.a(register_1_q), .b(4'b0001), .out(adder_1_out));  // open: cin, cout
  Register #(.width(4)) register_1 (.D(adder_1_out), .Q(register_1_q), .clk(clock_1_out), .clr(d_ff_1_q));  // open: en
  Comparator #(.width(4)) comparator_1 (.a(register_1_q), .b(delay), .gt(comparator_1_gt));  // open: eq, lt
  Register #(.width(4)) register_2 (.D(in_4bits), .Q(out_4bits), .clk(comparator_1_gt));  // open: en, clr
  D_Flip_Flop d_ff_1 (.D(comparator_1_gt), .Q(d_ff_1_q), .preset(clock_1_out));  // open: clk, Qn, en, reset
endmodule

module delay_1bit (
  input  in_1bit,
  input  [3:0] delay,
  output out_1bit1
);

  wire clock_1_out, comparator_1_gt, d_ff_1_q, not_1_out;
  wire [3:0] adder_1_out, register_1_q;

  Clock clock_1 (.out(clock_1_out));
  Adder #(.width(4)) adder_1 (.a(register_1_q), .b(4'b0001), .out(adder_1_out));  // open: cin, cout
  // Probe on register_1_q
  Register #(.width(4)) register_1 (.D(adder_1_out), .Q(register_1_q), .clk(clock_1_out), .clr(d_ff_1_q));  // open: en
  Comparator #(.width(4)) comparator_1 (.a(register_1_q), .b(delay), .gt(comparator_1_gt));  // open: eq, lt
  Register #(.width(1)) register_2 (.D(in_1bit), .Q(out_1bit1), .clk(not_1_out));  // open: en, clr
  not not_1 (not_1_out, comparator_1_gt);
  D_Flip_Flop d_ff_1 (.D(not_1_out), .Q(d_ff_1_q), .en(clock_1_out));  // open: clk, Qn, preset, reset
endmodule

module ctrl_rst_on (
  input  req_in,
  input  ack_out,
  input  rst,
  output ctrl_out,
  output req_out,
  output ack_in
);

  muller_rst_on muller_rst_on_1 (.A(req_in), .B(ack_out), .Reset(rst), .Z(ack_in));

  assign ctrl_out = ack_in;
  assign req_out = ack_in;
endmodule

module muller_rst_on (
  input  A,
  input  B,
  input  Reset,
  output Z
);

  wire and_1_out, and_2_out, multiplexer_1_out, multiplexer_2_out, not_1_out, not_2_out, or_1_out, or_2_out;

  Multiplexer multiplexer_1 (.in0(A), .in1(1'b1), .out(multiplexer_1_out), .sel(Reset));  // open: en
  Multiplexer multiplexer_2 (.in0(B), .in1(1'b0), .out(multiplexer_2_out), .sel(Reset));  // open: en
  not not_1 (not_1_out, multiplexer_2_out);
  and and_1 (and_1_out, multiplexer_1_out, not_1_out);
  or or_1 (or_1_out, multiplexer_1_out, not_1_out);
  or or_2 (or_2_out, and_1_out, and_2_out);
  and and_2 (and_2_out, or_2_out, or_1_out);
  not not_2 (not_2_out, Reset);
  and and_3 (Z, or_2_out, not_2_out);
endmodule

module network (
  input  data_in,
  input  req_in,
  input  data_in_2,
  input  req_in_2,
  input  sel,
  input  sel_2,
  input  sel_req,
  input  sel_req_2,
  input  rst,
  output data_out,
  output ack_in,
  output data_out_2,
  output ack_in_2,
  output sel_ack,
  output sel_ack_2
);

  wire data1, data2, data3, delay_1bit_1_out_1bit1, delay_1bit_2_out_1bit1, merge_1_ack_in1, merge_1_ack_in2,
       merge_1_req_out, multiplexer_1_out, neuron_1_data_out, neuron_1_req_out, neuron_2_req_out,
       neuron_3_ack_in, neuron_3_data_out, neuron_3_req_out, neuron_4_ack_in, neuron_4_req_out,
       neuron_5_ack_in, neuron_5_req_out, neuron_6_ack_in, neuron_6_req_out, neuron_7_ack_in,
       neuron_7_req_out, split_1_ack_in, split_1_req_out1, split_1_req_out2;

  neuron neuron_1 (
    .data_in(data_in), .req_in(req_in), .ack_in(ack_in), .data_out(neuron_1_data_out),
    .req_out(neuron_1_req_out), .ack_out(neuron_3_ack_in), .rst(rst));
  neuron neuron_2 (
    .data_in(data_in_2), .req_in(req_in_2), .ack_in(ack_in_2), .data_out(data1), .req_out(neuron_2_req_out),
    .ack_out(split_1_ack_in), .rst(rst));
  neuron neuron_3 (
    .data_in(neuron_1_data_out), .req_in(neuron_1_req_out), .ack_in(neuron_3_ack_in),
    .data_out(neuron_3_data_out), .req_out(neuron_3_req_out), .ack_out(neuron_4_ack_in), .rst(rst));
  split split_1 (
    .req_in(neuron_2_req_out), .sel(sel), .sel_req(sel_req), .ack_in(split_1_ack_in), .ack_sel(sel_ack),
    .req_out1(split_1_req_out1), .req_out2(split_1_req_out2), .ack_out1(neuron_6_ack_in),
    .ack_out2(neuron_5_ack_in), .rst(rst));
  neuron neuron_4 (
    .data_in(neuron_3_data_out), .req_in(neuron_3_req_out), .ack_in(neuron_4_ack_in), .data_out(data_out),
    .req_out(neuron_4_req_out), .ack_out(delay_1bit_1_out_1bit1), .rst(rst));
  neuron neuron_5 (
    .data_in(data1), .req_in(split_1_req_out1), .ack_in(neuron_5_ack_in), .data_out(data2),
    .req_out(neuron_5_req_out), .ack_out(merge_1_ack_in1), .rst(rst));
  neuron neuron_6 (
    .data_in(data1), .req_in(split_1_req_out2), .ack_in(neuron_6_ack_in), .data_out(data3),
    .req_out(neuron_6_req_out), .ack_out(merge_1_ack_in2), .rst(rst));
  delay_1bit delay_1bit_1 (.in_1bit(neuron_4_req_out), .delay(4'b1000), .out_1bit1(delay_1bit_1_out_1bit1));
  merge merge_1 (
    .req_in1(neuron_5_req_out), .sel(sel_2), .sel_req(sel_req_2), .req_in2(neuron_6_req_out),
    .ack_in1(merge_1_ack_in1), .req_out(merge_1_req_out), .sel_ack(sel_ack_2), .ack_in2(merge_1_ack_in2),
    .ack_out(neuron_7_ack_in), .rst(rst));
  Multiplexer #(.enable("false")) multiplexer_1 (.in0(data2), .in1(data3), .out(multiplexer_1_out), .sel(sel_2));
  neuron neuron_7 (
    .data_in(multiplexer_1_out), .req_in(merge_1_req_out), .ack_in(neuron_7_ack_in), .data_out(data_out_2),
    .req_out(neuron_7_req_out), .ack_out(delay_1bit_2_out_1bit1), .rst(rst));
  delay_1bit delay_1bit_2 (.in_1bit(neuron_7_req_out), .delay(4'b1000), .out_1bit1(delay_1bit_2_out_1bit1));

  // Other names for the same wires on the sheet: sel_ack_m = sel_ack_2; sel_ack_s = sel_ack; sel_m = sel_2;
  //   sel_req_m = sel_req_2; sel_req_s = sel_req; sel_s = sel
endmodule

module merge (
  input  req_in1,
  input  sel,
  input  sel_req,
  input  req_in2,
  input  ack_out,
  input  rst,
  output ack_in1,
  output req_out,
  output sel_ack,
  output ack_in2
);

  wire and_1_out, and_2_out, not_1_out, p_muller_1_z, p_muller_2_z;

  not not_1 (not_1_out, sel);
  and and_1 (and_1_out, sel, sel_req);
  and and_2 (and_2_out, sel_req, not_1_out);
  p_muller p_muller_1 (.A(req_in1), .B(and_1_out), .Reset(rst), .Z(p_muller_1_z));
  p_muller p_muller_2 (.A(and_2_out), .B(req_in2), .Reset(rst), .Z(p_muller_2_z));
  p_muller p_muller_3 (.A(ack_out), .B(p_muller_1_z), .Reset(rst), .Z(ack_in1));
  p_muller p_muller_4 (.A(p_muller_2_z), .B(ack_out), .Reset(rst), .Z(ack_in2));
  or or_1 (req_out, p_muller_1_z, p_muller_2_z);
  or or_2 (sel_ack, ack_in1, ack_in2);
endmodule

module split (
  input  req_in,
  input  sel,
  input  sel_req,
  input  ack_out1,
  input  ack_out2,
  input  rst,
  output req_out1,
  output req_out2,
  output ack_in,
  output ack_sel
);

  wire and_1_out, and_2_out, not_1_out;

  not not_1 (not_1_out, sel);
  and and_1 (and_1_out, sel, sel_req);
  and and_2 (and_2_out, sel_req, not_1_out);
  or or_1 (ack_in, ack_out1, ack_out2);
  p_muller p_muller_1 (.A(req_in), .B(and_1_out), .Reset(rst), .Z(req_out1));
  p_muller p_muller_2 (.A(and_2_out), .B(req_in), .Reset(rst), .Z(req_out2));

  assign ack_sel = ack_in;
endmodule
