// Logisim project muller.circ as structural Verilog: 1 circuit, main circuit main
module main (
  input  A,
  input  B,
  output Z
);

  wire and_1_out, and_2_out, or_1_out;

  and and_1 (and_1_out, A, B);
  or or_1 (or_1_out, A, B);
  or or_2 (Z, and_1_out, and_2_out);
  and and_2 (and_2_out, Z, or_1_out);
endmodule
