// Logisim project neuron_2.circ as structural Verilog: 2 circuits, main circuit main
module main (
  input  Req,
  input  Ack_out,
  input  [3:0] Coef,
  input  [3:0] Coef_2,
  input  [3:0] Data,
  output Req_out,
  output Ack,
  output [3:0] Data_out
);

  wire not_1_out, undriven_2;
  wire [3:0] adder_1_out, multiplexer_1_out, register_1_q, register_2_q, undriven;

  Register #(.width(4)) register_1 (.D(undriven), .Q(register_1_q));  // open: en, clk, clr
  Register #(.width(4)) register_2 (.D(Data), .Q(register_2_q), .clk(Req));  // open: en, clr
  muller muller_1 (.A(Req), .B(Ack_out), .Z(Ack));
  Adder #(.width(4)) adder_1 (.a(register_1_q), .b(register_2_q), .out(adder_1_out));  // open: cin, cout
  Multiplexer #(.width(4), .enable("false")) multiplexer_1 (
    .out(multiplexer_1_out), .sel(undriven_2));  // open: in0, in1
  Comparator #(.width(4), .mode("unsigned")) comparator_1 (.a(undriven), .b(Coef_2), .gt(Req_out));  // open: eq, lt
  not not_1 (not_1_out, Ack_out);
  Multiplexer #(.width(4), .enable("false")) multiplexer_2 (.in0(4'b0000), .in1(Coef), .out(Data_out), .sel(Req_out));
endmodule

module muller (
  input  A,
  input  B,
  output Z
);

  wire and_1_out, and_2_out, not_1_out, or_1_out;

  not not_1 (not_1_out, B);
  and and_1 (and_1_out, A, not_1_out);
  or or_1 (or_1_out, A, not_1_out);
  or or_2 (Z, and_1_out, and_2_out);
  and and_2 (and_2_out, Z, or_1_out);
endmodule
